// Logisim project lab7.circ as structural Verilog: 1 circuit, main circuit main
module main (
  input  A,
  input  B,
  input  Cin,
  output cout,
  output sum
);

  wire and_1_out, and_2_out, and_3_out, and_4_out, and_5_out, and_6_out, and_7_out, and_8_out, and_9_out,
       and_10_out, and_11_out, and_12_out, not_1_out, not_2_out, not_3_out, not_4_out, not_5_out, not_6_out,
       or_1_out, or_2_out;

  not not_1 (not_1_out, A);
  not not_2 (not_2_out, B);
  not not_3 (not_3_out, A);
  not not_4 (not_4_out, Cin);
  not not_5 (not_5_out, B);
  not not_6 (not_6_out, Cin);
  and and_1 (and_1_out, A, Cin);
  and and_2 (and_2_out, not_1_out, not_2_out);
  and and_3 (and_3_out, not_3_out, B);
  and and_4 (and_4_out, and_3_out, not_4_out);
  and and_5 (and_5_out, not_5_out, not_6_out);
  and and_6 (and_6_out, and_1_out, B);
  and and_7 (and_7_out, and_2_out, Cin);
  and and_8 (and_8_out, A, and_5_out);
  or or_1 (or_1_out, and_7_out, and_4_out);
  or or_2 (or_2_out, and_8_out, and_6_out);
  and and_9 (and_9_out, not_1_out, B, Cin);
  and and_10 (and_10_out, A, not_2_out, Cin);
  and and_11 (and_11_out, A, B, not_4_out);
  and and_12 (and_12_out, A, B, Cin);
  or or_3 (sum, or_1_out, or_2_out);
  or or_4 (cout, and_9_out, and_10_out, and_11_out, and_12_out);
endmodule
